# Fritzing sketch wordclock (saved by Fritzing 0.9.3b)
circuit board: 8.73045cm x 3.89486cm
breadboards: 1

parts:
  NEOPIXEL1 = Neopixel Strip -- Black (30/m) [part_number=1376]
  JACK1 = 2.1mm Barrel Jack with Terminal Block
  R1 = Resistor [tolerance=±5% resistance=330 package=THT]
  C1 = Electrolytic Capacitor [capacitance=1mF package="100 mil [THT, electrolytic]"]
  Part1 = Arduino Nano (Rev3.0) (ICSP)
  Part2 = Real Time Clock Module - DS1307 RTC Breakout Board
  R2 = Resistor [tolerance=±5% resistance=10k package=THT]
  DHT1 = DHT22 Humidity and Temperature Sensor
  S1 = Pushbutton [package="[SMD]"]
  S2 = Pushbutton [package="[SMD]"]
  S3 = Pushbutton [package="[SMD]"]
  Part3 = MCP9808 High Accuracy I2C Temperature Sensor [part_number=1782]
  R3 = Photocell (LDR) [package=THT]
  R4 = Resistor [tolerance=±5% resistance=10k package=THT]

nets:
  GND: NEOPIXEL1.GND, JACK1.NEG, C1.+, Part1.GND, Part2.GND, R2.Pin_0, DHT1.GND, Part3.GND, R4.Pin_1
  N1: NEOPIXEL1.Din, R1.Pin_0
  VDD: NEOPIXEL1.+5V, JACK1.POS, C1.-, Part1.VIN, Part2.5V, R2.Pin_1, DHT1.VDD, S1.Pin_3, S1.Pin_4, S2.Pin_3, S2.Pin_4, S3.Pin_3, S3.Pin_4, Part3.VDD, R3.pin_1
  N2: R1.Pin_1, Part1.D2, Part1.D10
  N3: Part1.D4, S1.Pin_1, S1.Pin_2
  N4: Part1.D5, S2.Pin_1, S2.Pin_2
  N5: Part1.D6, S3.Pin_1, S3.Pin_2
  N6: Part1.A5, Part2.SDA, Part3.SDA
  N7: Part1.A4, Part2.SCL, Part3.SCL
  N8: Part1.A2, DHT1.DATA
  N9: Part1.A1, R3.pin_0, R4.Pin_0

custom parts:
  Neopixel Strip -- Black (30/m): These NeoPixel strips have 30 digitally-addressable pixel LEDs per meter and are very affordable and are only 12.5 mm wide, 10 mm if you remove the strip from the casing.
  MCP9808 High Accuracy I2C Temperature Sensor: This I2C digital temperature sensor is one of the more accurate/precise we've ever seen, with a typical accuracy of ±0.25°C over the sensor's -40°C to +125°C range and precision of +0.0625°C. They work great with any microcontroller using standard i2c. There are 3 address pins so you can connect up to 8 to a single I2C bus without address collisions. Best of all, a wide voltage range makes is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
